# Fritzing sketch Arduino Shield Layout V2 (saved by Fritzing 0.9.1b)
circuit board: 5.00325cm x 5.27795cm

parts:
  J6 = female pin header, 8 pins [form="♀ (female)"]
  J1 = female pin header, 8 pins [form="♀ (female)"]
  J8 = female pin header, 6 pins [form="♀ (female)"]
  J4 = female pin header, 10 pins [form="♀ (female)"]
  J3 = female pin header, 10 pins [form="♀ (female)"]
  J2 = female pin header, 8 pins [form="♀ (female)"]
  J5 = female pin header, 8 pins [form="♀ (female)"]
  J7 = female pin header, 6 pins [form="♀ (female)"]

nets:
  N1: J6.pin1, J5.pin1
  IOREF: J6.pin2, J5.pin2
  RESET: J6.pin3, J5.pin3
  3.3V: J6.pin4, J5.pin4
  5V: J6.pin5, J5.pin5
  N2: J6.pin6, J6.pin7, J5.pin6, J5.pin7
  Vin: J6.pin8, J5.pin8
  D7: J1.pin1, J2.pin1
  ~D6: J1.pin2, J2.pin2
  ~D5: J1.pin3, J2.pin3
  D4: J1.pin4, J2.pin4
  ~D3: J1.pin5, J2.pin5
  D2: J1.pin6, J2.pin6
  D1: J1.pin7, J2.pin7
  D0: J1.pin8, J2.pin8
  A0: J8.pin1, J7.pin1
  A1: J8.pin2, J7.pin2
  A2: J8.pin3, J7.pin3
  A3: J8.pin4, J7.pin4
  A4: J8.pin5, J7.pin5
  A5: J8.pin6, J7.pin6
  SCL: J4.pin1, J3.pin1
  SDA: J4.pin2, J3.pin2
  AREF: J4.pin3, J3.pin3
  GND: J4.pin4, J3.pin4
  D13: J4.pin5, J3.pin5
  D12: J4.pin6, J3.pin6
  ~D11: J4.pin7, J3.pin7
  ~D10: J4.pin8, J3.pin8
  ~D9: J4.pin9, J3.pin9
  D8: J4.pin10, J3.pin10

notes:
  D0
  D1
  D2
  ~D3
  D4
  ~D5
  ~D6
  D7
  Vin
  GND
  5V
  3.3V
  RESET
  IOREF
  D8
  A0
  A5
  D13
  AREF
  SDA
  SCL
  A1
  A2
  A3
  A4
  ~D9
  ~D10
  ~D11
  D12
