# Fritzing sketch Arduino Shield Layout (saved by Fritzing 0.8.7b)
circuit board: 4.50694cm x 5.2093cm
breadboards: 1

parts:
  J2 = female pin header, 8 pins [form="♀ (female)"]
  J1 = female pin header, 8 pins [form="♀ (female)"]
  J3 = female pin header, 8 pins [form="♀ (female)"]
  J4 = female pin header, 6 pins [form="♀ (female)"]
  J5 = female pin header, 8 pins [form="♀ (female)"]
  J6 = female pin header, 8 pins [form="♀ (female)"]
  J7 = female pin header, 8 pins [form="♀ (female)"]
  J8 = female pin header, 6 pins [form="♀ (female)"]

nets:
  N1: J2.pin1, J5.pin1
  N2: J2.pin2, J5.pin2
  N3: J2.pin3, J5.pin3
  N4: J2.pin4, J5.pin4
  N5: J2.pin5, J5.pin5
  N6: J2.pin6, J5.pin6
  N7: J2.pin7, J5.pin7
  N8: J2.pin8, J5.pin8
  N9: J1.pin1, J6.pin1
  N10: J1.pin2, J6.pin2
  N11: J1.pin3, J6.pin3
  N12: J1.pin4, J6.pin4
  N13: J1.pin5, J6.pin5
  N14: J1.pin6, J6.pin6
  N15: J1.pin7, J6.pin7
  N16: J1.pin8, J6.pin8
  N17: J3.pin1, J7.pin1
  N18: J3.pin2, J7.pin2
  N19: J3.pin3, J7.pin3
  N20: J3.pin4, J7.pin4
  N21: J3.pin5, J7.pin5
  N22: J3.pin6, J7.pin6
  N23: J3.pin7, J7.pin7
  N24: J3.pin8, J7.pin8
  N25: J4.pin1, J8.pin1
  N26: J4.pin2, J8.pin2
  N27: J4.pin3, J8.pin3
  N28: J4.pin4, J8.pin4
  N29: J4.pin5, J8.pin5
  N30: J4.pin6, J8.pin6
