# Fritzing sketch 16Motors+595+L298 (saved by Fritzing 0.8.7b)
breadboards: 1

parts:
  U3 = L298 [package=multiwatt15]
  IC1 = SHIFT REGISTER [package=dil16]
  IC2 = SHIFT REGISTER [package=dil16]
  IC3 = SHIFT REGISTER [package=dil16]
  Part1 = Arduino Uno (Rev3)

nets:
  GND: U3.CSA, U3.GND, U3.CSB
  N1: U3.IN1, IC2.QA
  N2: U3.ENA, IC2.QC
  N3: U3.IN2, IC2.QB
  N4: U3.IN3, IC2.QD
  N5: U3.ENB, IC2.QF
  N6: U3.IN4, IC2.QE
  N7: IC1.QH*, IC3.SER
  N8: IC1.SER, IC2.QH*
  N9: IC2.SCL, Part1.D4
  N10: IC2.SCK, Part1.D3_PWM
  N11: IC2.RCK, Part1.D5_PWM
  N12: IC2.G, Part1.D6_PWM
  N13: IC2.SER, Part1.D2
