# Fritzing sketch 16Motors+595+MOSFETs (saved by Fritzing 0.8.7b)
breadboards: 1

parts:
  IC1 = SHIFT REGISTER [package=dil16]
  IC2 = SHIFT REGISTER [package=dil16]
  IC3 = SHIFT REGISTER [package=dil16]
  Part1 = Arduino Uno (Rev3)
  Q2 = Basic FET N-Channel [package="TO220 [THT]"]
  Q5 = Basic FET N-Channel [package="D2Pak [SMD]"]  # not connected
  Q7 = MOSFET-NCHANNEL [package=to220v]  # not connected
  Q8 = Basic FET N-Channel [package="DPak [SMD]"]  # not connected
  Power_plug1 = Power plug
  LED1 = LED - 5mm [color="Red (633nm)" package="5 mm [THT]"]
  J1 = Screw terminal - 2 pins [package=THT]
  R1 = Resistor [tolerance=±5% resistance=220 package=THT]
  Q9 = Basic FET N-Channel [package="TO220 [THT]"]
  Q10 = Basic FET N-Channel [package="D2Pak [SMD]"]  # not connected
  LED2 = LED - 5mm [color="Red (633nm)" package="5 mm [THT]"]
  J2 = Screw terminal - 2 pins [package=THT]
  R2 = Resistor [tolerance=±5% resistance=220 package=THT]
  Q11 = Basic FET N-Channel [package="TO220 [THT]"]
  LED3 = LED - 5mm [color="Red (633nm)" package="5 mm [THT]"]
  J3 = Screw terminal - 2 pins [package=THT]
  R3 = Resistor [tolerance=±5% resistance=220 package=THT]
  Q12 = Basic FET N-Channel [package="TO220 [THT]"]
  Q13 = Basic FET N-Channel [package="TO220 [THT]"]
  Q14 = Basic FET N-Channel [package="TO220 [THT]"]
  LED4 = LED - 5mm [color="Red (633nm)" package="5 mm [THT]"]
  LED5 = LED - 5mm [color="Red (633nm)" package="5 mm [THT]"]
  LED6 = LED - 5mm [color="Red (633nm)" package="5 mm [THT]"]
  J4 = Screw terminal - 2 pins [package=THT]
  J5 = Screw terminal - 2 pins [package=THT]
  J6 = Screw terminal - 2 pins [package=THT]
  R4 = Resistor [tolerance=±5% resistance=220 package=THT]
  R5 = Resistor [tolerance=±5% resistance=220 package=THT]
  R6 = Resistor [tolerance=±5% resistance=220 package=THT]
  Q15 = Basic FET N-Channel [package="TO220 [THT]"]
  Q16 = Basic FET N-Channel [package="TO220 [THT]"]
  Q17 = Basic FET N-Channel [package="TO220 [THT]"]
  Q18 = Basic FET N-Channel [package="TO220 [THT]"]
  Q19 = Basic FET N-Channel [package="TO220 [THT]"]
  LED7 = LED - 5mm [color="Red (633nm)" package="5 mm [THT]"]
  LED8 = LED - 5mm [color="Red (633nm)" package="5 mm [THT]"]
  LED9 = LED - 5mm [color="Red (633nm)" package="5 mm [THT]"]
  LED10 = LED - 5mm [color="Red (633nm)" package="5 mm [THT]"]
  LED11 = LED - 5mm [color="Red (633nm)" package="5 mm [THT]"]
  J7 = Screw terminal - 2 pins [package=THT]
  J8 = Screw terminal - 2 pins [package=THT]
  J9 = Screw terminal - 2 pins [package=THT]
  J10 = Screw terminal - 2 pins [package=THT]
  J11 = Screw terminal - 2 pins [package=THT]
  R7 = Resistor [tolerance=±5% resistance=220 package=THT]  # not connected
  R8 = Resistor [tolerance=±5% resistance=220 package=THT]
  R9 = Resistor [tolerance=±5% resistance=220 package=THT]  # not connected
  R10 = Resistor [tolerance=±5% resistance=220 package=THT]
  R11 = Resistor [tolerance=±5% resistance=220 package=THT]  # not connected

nets:
  GND: IC1.GND, IC1.G, IC2.GND, IC2.G, IC3.GND, IC3.G, Part1.GND, Q2.source, Power_plug1.GND, R1.Pin_1, Q9.source, R2.Pin_1, Q11.source, R3.Pin_1, Q12.source, Q13.source, Q14.source, R4.Pin_1, R5.Pin_1, R6.Pin_1, Q16.source, Q17.source, J7.pin1, R8.Pin_1, R10.Pin_1
  N1: IC1.QH*, IC3.SER
  VCC: IC1.SCL, IC2.SCL, IC2.VCC, IC3.SCL, Part1.5V
  N2: IC1.SCK, IC2.SCK, IC3.SCK, Part1.D12/MISO
  N3: IC1.RCK, IC2.RCK, IC3.RCK, Part1.D8
  N4: IC1.SER, IC2.QH*
  N5: IC2.QB, Q9.gate
  N6: IC2.QC, Q11.gate
  N7: IC2.QD, Q12.gate
  N8: IC2.QE, Q13.gate
  N9: IC2.QF, Q14.gate
  N10: IC2.QG, Q16.gate
  N11: IC2.QH, Q18.gate
  N12: IC2.SER, Part1.D11_PWM/MOSI
  N13: IC2.QA, Q2.gate
  N14: Q2.drain, LED1.anode, J1.pin2
  N15: Power_plug1.VCC, J1.pin1, J2.pin1, J3.pin1, J4.pin1, J5.pin1, J6.pin1, J10.pin1, J11.pin1
  N16: LED1.cathode, R1.Pin_0
  N17: Q9.drain, LED2.anode, J2.pin2
  N18: Q11.drain, LED3.anode, J3.pin2
  N19: LED3.cathode, R3.Pin_0
  N20: Q12.drain, LED4.anode, J4.pin2
  N21: Q13.drain, LED6.anode, J5.pin2
  N22: Q14.drain, LED5.anode, J6.pin2
  N23: Q15.drain, LED9.anode, J8.pin2
  N24: Q16.drain, LED11.anode, J7.pin2
  N25: Q17.drain, LED7.anode, J10.pin2
  N26: Q18.drain, LED10.anode, J11.pin2
  N27: Q19.drain, LED8.anode, J9.pin2
