# Fritzing sketch 16Motors+MOSFETs+commonMotorLeadBussed (saved by Fritzing 0.8.7b)
breadboards: 1

parts:
  Q2 = Basic FET N-Channel [package="TO220 [THT]"]
  LED1 = LED - 5mm [color="Red (633nm)" package="5 mm [THT]"]
  R1 = Resistor [tolerance=±5% resistance=1k package=THT]
  Q9 = Basic FET N-Channel [package="TO220 [THT]"]
  LED2 = LED - 5mm [color="Red (633nm)" package="5 mm [THT]"]
  R2 = Resistor [tolerance=±5% resistance=1k package=THT]
  Q11 = Basic FET N-Channel [package="TO220 [THT]"]
  LED3 = LED - 5mm [color="Red (633nm)" package="5 mm [THT]"]
  R3 = Resistor [tolerance=±5% resistance=220 package=THT]
  Q12 = Basic FET N-Channel [package="TO220 [THT]"]
  Q13 = Basic FET N-Channel [package="TO220 [THT]"]
  Q14 = Basic FET N-Channel [package="TO220 [THT]"]
  LED4 = LED - 5mm [color="Red (633nm)" package="5 mm [THT]"]
  LED5 = LED - 5mm [color="Red (633nm)" package="5 mm [THT]"]
  LED6 = LED - 5mm [color="Red (633nm)" package="5 mm [THT]"]
  R4 = Resistor [tolerance=±5% resistance=220 package=THT]
  R5 = Resistor [tolerance=±5% resistance=220 package=THT]
  R6 = Resistor [tolerance=±5% resistance=220 package=THT]
  Q15 = Basic FET N-Channel [package="TO220 [THT]"]
  Q16 = Basic FET N-Channel [package="TO220 [THT]"]
  Q17 = Basic FET N-Channel [package="TO220 [THT]"]
  Q18 = Basic FET N-Channel [package="TO220 [THT]"]
  Q19 = Basic FET N-Channel [package="TO220 [THT]"]
  LED7 = LED - 5mm [color="Red (633nm)" package="5 mm [THT]"]
  LED8 = LED - 5mm [color="Red (633nm)" package="5 mm [THT]"]
  LED9 = LED - 5mm [color="Red (633nm)" package="5 mm [THT]"]
  LED10 = LED - 5mm [color="Red (633nm)" package="5 mm [THT]"]
  LED11 = LED - 5mm [color="Red (633nm)" package="5 mm [THT]"]
  R7 = Resistor [tolerance=±5% resistance=220 package=THT]
  R8 = Resistor [tolerance=±5% resistance=220 package=THT]
  R9 = Resistor [tolerance=±5% resistance=220 package=THT]
  R10 = Resistor [tolerance=±5% resistance=220 package=THT]
  R11 = Resistor [tolerance=±5% resistance=220 package=THT]
  Part2 = Arduino Prototyping Shield
  J12 = Screw terminal - 2 pins [package=THT]
  J1 = screw terminal, 17 pins
  J5 = screw terminal, 4 pins [part_number="rotary encoder"]

nets:
  N1: Q2.gate, Part2.D13
  N2: Q2.drain, LED1.anode, J1.pin2
  GND: Q2.source, R1.Pin_1, Q9.source, R2.Pin_1, Q11.source, R3.Pin_1, Q12.source, Q13.source, Q14.source, R4.Pin_1, R5.Pin_1, R6.Pin_1, Q15.source, Q16.source, Q17.source, Q18.source, Q19.source, R7.Pin_1, R8.Pin_1, R9.Pin_1, R10.Pin_1, R11.Pin_1, Part2.GND, J12.pin2, J5.pin4
  N3: LED1.cathode, R1.Pin_0
  N4: Q9.gate, Part2.D12
  N5: Q9.drain, LED2.anode, J1.pin3
  N6: Q11.gate, Part2.D11
  N7: Q11.drain, LED3.anode, J1.pin4
  N8: LED3.cathode, R3.Pin_0
  N9: Q12.gate, Part2.D10
  N10: Q12.drain, LED4.anode, J1.pin5
  N11: Q13.gate, Part2.D9
  N12: Q13.drain, LED6.anode, J1.pin6
  N13: Q14.gate, Part2.D8
  N14: Q14.drain, LED5.anode, J1.pin7
  N15: Q15.gate, Part2.D5
  N16: Q15.drain, LED9.anode, J1.pin10
  N17: Q16.gate, Part2.D7
  N18: Q16.drain, LED11.anode, J1.pin8
  N19: Q17.gate, Part2.A5
  N20: Q17.drain, LED7.anode, J1.pin12
  N21: Q18.gate, Part2.D6
  N22: Q18.drain, LED10.anode, J1.pin9
  N23: Q19.gate, Part2.D4
  N24: Q19.drain, LED8.anode, J1.pin11
  N25: Part2.+9V, J5.pin1
  N26: Part2.D2, J5.pin3
  N27: Part2.D3, J5.pin2
  N28: J12.pin1, J1.pin1

notes:
  + 12 VDC
  GND
  Motor Common (black wire)
  motor blue wires
  5 more MOSFETs going to A0 through A4
