# Fritzing sketch 16Motors+MOSFETs+individualScrewTerminals (saved by Fritzing 0.8.7b)
breadboards: 1

parts:
  Q2 = Basic FET N-Channel [package="TO220 [THT]"]
  LED1 = LED - 5mm [color="Red (633nm)" package="5 mm [THT]"]
  J1 = Screw terminal - 2 pins [package=THT]
  R1 = Resistor [tolerance=±5% resistance=1k package=THT]
  Q9 = Basic FET N-Channel [package="TO220 [THT]"]
  LED2 = LED - 5mm [color="Red (633nm)" package="5 mm [THT]"]
  J2 = Screw terminal - 2 pins [package=THT]
  R2 = Resistor [tolerance=±5% resistance=1k package=THT]
  Q11 = Basic FET N-Channel [package="TO220 [THT]"]
  LED3 = LED - 5mm [color="Red (633nm)" package="5 mm [THT]"]
  J3 = Screw terminal - 2 pins [package=THT]
  R3 = Resistor [tolerance=±5% resistance=220 package=THT]
  Q12 = Basic FET N-Channel [package="TO220 [THT]"]
  Q13 = Basic FET N-Channel [package="TO220 [THT]"]
  Q14 = Basic FET N-Channel [package="TO220 [THT]"]
  LED4 = LED - 5mm [color="Red (633nm)" package="5 mm [THT]"]
  LED5 = LED - 5mm [color="Red (633nm)" package="5 mm [THT]"]
  LED6 = LED - 5mm [color="Red (633nm)" package="5 mm [THT]"]
  J4 = Screw terminal - 2 pins [package=THT]
  J5 = Screw terminal - 2 pins [package=THT]
  J6 = Screw terminal - 2 pins [package=THT]
  R4 = Resistor [tolerance=±5% resistance=220 package=THT]
  R5 = Resistor [tolerance=±5% resistance=220 package=THT]
  R6 = Resistor [tolerance=±5% resistance=220 package=THT]
  Q15 = Basic FET N-Channel [package="TO220 [THT]"]
  Q16 = Basic FET N-Channel [package="TO220 [THT]"]
  Q17 = Basic FET N-Channel [package="TO220 [THT]"]
  Q18 = Basic FET N-Channel [package="TO220 [THT]"]
  Q19 = Basic FET N-Channel [package="TO220 [THT]"]
  LED7 = LED - 5mm [color="Red (633nm)" package="5 mm [THT]"]
  LED8 = LED - 5mm [color="Red (633nm)" package="5 mm [THT]"]
  LED9 = LED - 5mm [color="Red (633nm)" package="5 mm [THT]"]
  LED10 = LED - 5mm [color="Red (633nm)" package="5 mm [THT]"]
  LED11 = LED - 5mm [color="Red (633nm)" package="5 mm [THT]"]
  J7 = Screw terminal - 2 pins [package=THT]
  J8 = Screw terminal - 2 pins [package=THT]
  J9 = Screw terminal - 2 pins [package=THT]
  J10 = Screw terminal - 2 pins [package=THT]
  J11 = Screw terminal - 2 pins [package=THT]
  R7 = Resistor [tolerance=±5% resistance=220 package=THT]
  R8 = Resistor [tolerance=±5% resistance=220 package=THT]
  R9 = Resistor [tolerance=±5% resistance=220 package=THT]
  R10 = Resistor [tolerance=±5% resistance=220 package=THT]
  R11 = Resistor [tolerance=±5% resistance=220 package=THT]
  Part2 = Arduino Prototyping Shield
  J12 = Screw terminal - 2 pins [package=THT]

nets:
  N1: Q2.gate, Part2.D13
  N2: Q2.drain, LED1.anode, J1.pin2
  GND: Q2.source, R1.Pin_1, Q9.source, R2.Pin_1, Q11.source, R3.Pin_1, Q13.source, Q14.source, R4.Pin_1, R5.Pin_1, R6.Pin_1, Q15.source, Q16.source, Q17.source, Q18.source, Q19.source, J7.pin1, R7.Pin_1, R8.Pin_1, R9.Pin_1, R10.Pin_1, R11.Pin_1, J12.pin2
  N3: LED1.cathode, R1.Pin_0
  N4: J1.pin1, J2.pin1, J3.pin1, J4.pin1, J5.pin1, J6.pin1, J8.pin1, J9.pin1, J10.pin1, J11.pin1, J12.pin1
  N5: Q9.gate, Part2.D12
  N6: Q9.drain, LED2.anode, J2.pin2
  N7: Q11.gate, Part2.D11
  N8: Q11.drain, LED3.anode, J3.pin2
  N9: LED3.cathode, R3.Pin_0
  N10: Q12.gate, Part2.D10
  N11: Q12.drain, LED4.anode, J4.pin2
  N12: Q13.gate, Part2.D9
  N13: Q13.drain, LED6.anode, J5.pin2
  N14: Q14.gate, Part2.D8
  N15: Q14.drain, LED5.anode, J6.pin2
  N16: Q15.gate, Part2.D5
  N17: Q15.drain, LED9.anode, J8.pin2
  N18: Q16.gate, Part2.D7
  N19: Q16.drain, LED11.anode, J7.pin2
  N20: Q17.gate, Part2.A5
  N21: Q17.drain, LED7.anode, J10.pin2
  N22: Q18.gate, Part2.D6
  N23: Q18.drain, LED10.anode, J11.pin2
  N24: Q19.gate, Part2.D4
  N25: Q19.drain, LED8.anode, J9.pin2

notes:
  + 12 VDC
  GND
  Motor
