# Fritzing sketch 16x2_LCD (saved by Fritzing 0.8.7b)
breadboards: 1

parts:
  Part1 = Arduino Uno (Rev3)
  U2 = LCD-16X2 [package=lcd-16x2_noholes]
  R1 = Resistor [tolerance=±5% resistance=220 package=THT]
  R4 = TRIMPOT [part_number=10K package=3362u-2]

nets:
  N1: Part1.D11_PWM/MOSI, U2.E
  N2: Part1.D12/MISO, U2.RS
  N3: Part1.D2, U2.DB7
  N4: Part1.D3_PWM, U2.DB6
  N5: Part1.D4, U2.DB5
  N6: Part1.D5_PWM, U2.DB4
  5V: Part1.5V, U2.VDD, R1.Pin_0, R4.CCW
  GND: Part1.GND, U2.VSS, U2.R_W, U2.K, R4.CW
  N7: U2.VO, R4.WIPER
  N8: U2.A, R1.Pin_1
