# Fritzing sketch 555DigitalPot (saved by Fritzing 0.9.3b)
circuit board: 3.5883cm x 1.44506cm
breadboards: 1

parts:
  J1 = Piezo Speaker
  R2 = Resistor [tolerance=±5% resistance=10k package=THT]
  C1 = Ceramic Capacitor [capacitance=100nF package="100 mil [THT, multilayer]"]
  C2 = Electrolytic Capacitor [capacitance=10µF package="100 mil [THT, electrolytic]"]
  U1 = 555 Timer [package="DIP8 [THT]"]
  R4 = Resistor [tolerance=±5% resistance=1k package=THT]
  IC1 = IC, DIP package, 8 pins [chip_label=IC]
  Part1 = Arduino Uno (Rev3)

nets:
  N1: J1.pin1, C2.-
  GND: J1.pin2, U1.Ground, IC1.pin4, Part1.GND
  N2: R2.Pin_0, U1.Discharge, IC1.pin5
  N3: R2.Pin_1, C1.1, U1.Trigger, U1.Threshold
  N4: C2.+, U1.Output
  N5: U1.Reset, U1.Vcc_Supply_Voltage, R4.Pin_0, IC1.pin8, Part1.5V
  N6: R4.Pin_1, IC1.pin6
  N7: IC1.pin1, Part1.D10_PWM/SS
  N8: IC1.pin2, Part1.D13/SCK
  N9: IC1.pin3, Part1.D11_PWM/MOSI

notes:
  Piezo Speaker
