# Fritzing sketch 74HC4052_74HC595Shield (saved by Fritzing 0.9.2b)
circuit board: 6.88566cm x 5.36311cm
breadboards: 1

parts:
  IC1 = SHIFT REGISTER [package=dil16]
  U2 = 74HC4052 [package=dil16]
  R1 = Resistor [tolerance=±5% resistance=220 package=THT]
  J1 = female pin header, 3 pins [form="♀ (female)"]
  J2 = female pin header, 3 pins [form="♀ (female)"]
  J3 = female pin header, 3 pins [form="♀ (female)"]
  J4 = female pin header, 3 pins [form="♀ (female)"]
  R2 = Resistor [tolerance=±5% resistance=220 package=THT]
  R3 = Resistor [tolerance=±5% resistance=220 package=THT]
  LED3 = LED - 5mm [color="Red (633nm)" package="5 mm [THT]"]
  R4 = Resistor [tolerance=±5% resistance=220 package=THT]
  LED4 = LED - 5mm [color="Red (633nm)" package="5 mm [THT]"]
  R5 = Resistor [tolerance=±5% resistance=220 package=THT]
  LED5 = LED - 5mm [color="Red (633nm)" package="5 mm [THT]"]
  R6 = Resistor [tolerance=±5% resistance=220 package=THT]
  LED6 = LED - 5mm [color="Red (633nm)" package="5 mm [THT]"]
  R7 = Resistor [tolerance=±5% resistance=220 package=THT]
  LED7 = LED - 5mm [color="Red (633nm)" package="5 mm [THT]"]
  R8 = Resistor [tolerance=±5% resistance=220 package=THT]
  LED8 = LED - 5mm [color="Red (633nm)" package="5 mm [THT]"]
  LED2 = LED - 5mm [color="Red (633nm)" package="5 mm [THT]"]
  LED1 = LED - 5mm [color="Red (633nm)" package="5 mm [THT]"]
  Part1 = Arduino Uno (Rev3)

nets:
  N1: IC1.QB, R7.Pin_0
  N2: IC1.QC, R1.Pin_0
  N3: IC1.QD, R6.Pin_0
  N4: IC1.QE, R5.Pin_0
  N5: IC1.QF, R4.Pin_0
  N6: IC1.QG, R3.Pin_0
  N7: IC1.QH, R2.Pin_0
  GND: IC1.GND, IC1.G, U2.INH, U2.VEE, U2.GND, J1.pin3, J2.pin3, J3.pin3, J4.pin3, LED3.cathode, LED4.cathode, LED5.cathode, LED6.cathode, LED7.cathode, LED8.cathode, LED2.cathode, LED1.cathode, Part1.GND
  5V: IC1.SCL, IC1.VCC, U2.VCC, J1.pin1, J2.pin1, J3.pin1, J4.pin1, Part1.5V
  N8: IC1.SCK, Part1.D11_PWM/MOSI
  N9: IC1.RCK, Part1.D12/MISO
  N10: IC1.SER, Part1.D10_PWM/SS
  N11: IC1.QA, R8.Pin_0
  N12: U2.Y, Part1.A1
  N13: U2.B, Part1.D4
  N14: U2.A, Part1.D2
  N15: U2.X3, J2.pin2
  N16: U2.X0, J1.pin2
  N17: U2.X, Part1.A0
  N18: U2.X1, J4.pin2
  N19: U2.X2, J3.pin2
  N20: R1.Pin_1, LED1.anode
  N21: R2.Pin_1, LED2.anode
  N22: R3.Pin_1, LED3.anode
  N23: R4.Pin_1, LED4.anode
  N24: R5.Pin_1, LED5.anode
  N25: R6.Pin_1, LED6.anode
  N26: R7.Pin_1, LED7.anode
  N27: R8.Pin_1, LED8.anode
