# Fritzing sketch AdafruitMotorShieldSeparatePower (saved by Fritzing 0.9.3b)

parts:
  Part2 = Adafruit Motor/Stepper/Servo Shield [part_number="Adafruit #1438"]
  M1 = DC Motor
  M2 = DC Motor
  Part3 = Arduino Uno (Rev3)  # not connected
  VCC2 = Battery block 9V  # not connected
  C1 = Electrolytic Capacitor [capacitance=1µF package="100 mil [THT, electrolytic]"]  # not connected
  VCC1 = 4 x AAA Battery Mount

nets:
  N1: Part2.M3A, M2.pin_2
  N2: Part2.M3B, M2.pin_1
  N3: Part2.M4B, M1.pin_2
  N4: Part2.M4A, M1.pin_1
  N5: Part2.GND, VCC1.-
  N6: Part2.VMOTOR, VCC1.+

notes:
  REMOVE VIN JUMPER!
  7-12V for Arduino
  5-12V for motor(s)

custom parts:
  Adafruit Motor/Stepper/Servo Shield: The original Adafruit Motorshield kit is one of our most beloved kits, which is why we decided to make something even better. We have upgraded the shield kit to make the bestest, easiest way to drive DC and Stepper motors. This shield will make quick work of your next robotics project! We kept the ability to drive up to 4 DC motors or 2 stepper motors, but added many improvements: Instead of a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
