# Fritzing sketch BJTTransistorSwitch (saved by Fritzing 0.8.7b)
circuit board: 6.88566cm x 5.36311cm
breadboards: 2

parts:
  Transistor_switch = npn-Powertransistor [package="TO220 [THT]"]
  Base_resistor = Resistor [resistance=1k tolerance=±5% package=THT]
  Arduino_or_any_other_controller = Arduino Uno (Rev3)
  Motor_or_other_load = DC Motor

nets:
  N1: Transistor_switch.base, Base_resistor.Pin_1
  N2: Transistor_switch.collector, Motor_or_other_load.pin_2
  N3: Transistor_switch.emitter, Arduino_or_any_other_controller.GND
  N4: Base_resistor.Pin_0, Arduino_or_any_other_controller.D9_PWM
  N5: Arduino_or_any_other_controller.VIN, Motor_or_other_load.pin_1

notes:
  Using a power transistor with an Arduino will allow you to control outputs that need more current or higher voltages than the Arduino can provide. Related example: http://itp.nyu.edu/physcomp/
  Tutorials/HighCurrentLoads

// code stored in the sketch: npnPowerTransistor.ino
const int transistorPin = 9;    // connected to the base of the transistor

 void setup() {
   // set  the transistor pin as output:
   pinMode(transistorPin, OUTPUT);
 }

 void loop() {
   digitalWrite(transistorPin, HIGH);
   delay(1000);
   digitalWrite(transistorPin, LOW);
   delay(1000);
 }
