# Fritzing sketch BLE_andMiscShield (saved by Fritzing 0.9.3b)
circuit board: 5.50559cm x 5.49894cm
breadboards: 1

parts:
  Part1 = Arduino Uno (Rev3)
  R4 = TRIMPOT [package=3386u]
  LED3 = LED - 5mm [color="Green (560nm)" package="5 mm [THT]"]
  J1 = Camdenboss CTB0158-2 [part_number=CTB0158-2 package=THT]
  J2 = female pin header, 3 pins [form="♀ (female)"]
  Bluefruit_SPI_Friend = female pin header, 9 pins [form="♀ (female)"]
  R5 = Resistor [tolerance=±5% resistance=220 package=THT]
  S1 = Taiway 100-SP-X-T1 SPDT Miniature Toggle Switch [part_number=100-SP-X-T1-0-0-B1-M1 package=THT]

nets:
  N1: Part1.A0, R4.WIPER
  N2: Part1.D8, Bluefruit_SPI_Friend.pin6
  N3: Part1.D11_PWM/MOSI, Bluefruit_SPI_Friend.pin7
  N4: Part1.D12/MISO, Bluefruit_SPI_Friend.pin8
  N5: Part1.D13/SCK, Bluefruit_SPI_Friend.pin9
  GND: Part1.GND, R4.CW, J1.pin1, J2.pin3, Bluefruit_SPI_Friend.pin2, R5.Pin_1
  N6: Part1.D2, J2.pin1
  N7: Part1.D3_PWM, LED3.anode
  N8: Part1.D4, Bluefruit_SPI_Friend.pin3
  N9: Part1.D7, Bluefruit_SPI_Friend.pin5
  5V: Part1.5V, R4.CCW, Bluefruit_SPI_Friend.pin1
  N10: LED3.cathode, R5.Pin_0
  N11: J1.pin2, S1.L2
  N12: J2.pin2, S1.COM

notes:
  signal
  5V servo
