# Fritzing sketch arduinoLDRLED (saved by Fritzing 0.9.2b)
breadboards: 1

parts:
  Arduino1 = Arduino Uno (Rev3)
  R2 = Resistor [tolerance=±5% resistance=10k package=THT]
  R1 = Photocell (LDR) [package=THT]
  LED1 = LED - 5mm [color="Red (633nm)" package="5 mm [THT]"]
  R3 = Resistor [tolerance=±5% resistance=1k package=THT]

nets:
  N1: Arduino1.A0, R2.Pin_0, R1.pin_0
  N2: Arduino1.D3_PWM, LED1.anode
  N3: Arduino1.5V, R1.pin_1
  N4: Arduino1.GND, R2.Pin_1, R3.Pin_1
  N5: LED1.cathode, R3.Pin_0
