# Fritzing sketch arduinoWireSwitch (saved by Fritzing 0.9.1b)
breadboards: 1

parts:
  Arduino1 = Arduino Uno (Rev3)
  R2 = Resistor [tolerance=±5% resistance=10k package=THT]

nets:
  white wire: Arduino1.A0, R2.Pin_0
  blue wire: Arduino1.5V
  N1: Arduino1.GND, R2.Pin_1
