# Fritzing sketch screwTerminalDigitalInput (saved by Fritzing 0.9.3b)
breadboards: 1

parts:
  Part1 = Arduino Uno (Rev3)
  R1 = Resistor [tolerance=±5% resistance=10k package=THT]
  J2 = Camdenboss CTB0158-2 [part_number=CTB0158-2 package=THT]

nets:
  N1: Part1.GND, R1.Pin_1
  N2: Part1.D0/RX, R1.Pin_0, J2.pin2
  N3: Part1.3V3, J2.pin1

notes:
  screw terminal
  for switch
