# Fritzing sketch trivialDoubleSidedShield (saved by Fritzing 0.9.2b)
circuit board: 6.88566cm x 5.36311cm
breadboards: 1

parts:
  Part1 = Arduino Uno (Rev3)
  LED1 = LED - 5mm [color="Red (633nm)" package="5 mm [THT]"]
  R1 = Resistor [tolerance=±5% resistance=220 package=THT]
  LED2 = LED - 5mm [color="Red (633nm)" package="5 mm [THT]"]
  R2 = Resistor [tolerance=±5% resistance=220 package=THT]

nets:
  N1: Part1.D13/SCK, LED1.cathode
  N2: Part1.GND, R1.Pin_1, R2.Pin_1
  N3: LED1.anode, R1.Pin_0
  N4: LED2.anode, R2.Pin_0
