# Fritzing sketch IRReceiver (saved by Fritzing 0.8.7b)
breadboards: 1

parts:
  Part1 = Arduino Uno (Rev3)
  IR1 = TSOP312.., 314.. [package=THT]

nets:
  N1: Part1.D11_PWM/MOSI, IR1.GND
  N2: Part1.5V, IR1.Data
  N3: Part1.GND, IR1.Vs
