# Fritzing sketch L298H-BridgeSeparatePower (saved by Fritzing 0.9.3b)

parts:
  M1 = DC Motor
  M2 = DC Motor
  Part3 = Arduino Uno (Rev3)
  VCC2 = Battery block 9V  # not connected
  C1 = Electrolytic Capacitor [capacitance=1µF package="100 mil [THT, electrolytic]"]  # not connected
  VCC1 = 4 x AAA Battery Mount
  S1 = H-Bridge with L298N

nets:
  N1: M1.pin_1, S1.M2-02
  N2: M1.pin_2, S1.M2-01
  N3: M2.pin_1, S1.M1-02
  N4: M2.pin_2, S1.M1-01
  N5: Part3.D11_PWM/MOSI, S1.ENA
  N6: Part3.D12/MISO, S1.IN2
  N7: Part3.D13/SCK, S1.IN1
  GND: Part3.GND, VCC1.-, S1.GND
  N8: Part3.D2, S1.IN3
  N9: Part3.D3_PWM, S1.ENB
  N10: Part3.D4, S1.IN4
  N11: VCC1.+, S1.12V

notes:
  7-12V for Arduino
  7.5-46V for motor(s)
  to join wires
  Use wire nut

custom parts:
  H-Bridge with L298N: h-bridge
