# Fritzing sketch TB6560_pot_LCD (saved by Fritzing 0.9.2b)
breadboards: 1

parts:
  Part1 = Arduino Uno (Rev3)
  U2 = LCD-16X2 [package=lcd-16x2_noholes]
  R1 = Resistor [tolerance=±5% resistance=220 package=THT]
  R4 = TRIMPOT [part_number=10K package=3362u-2]
  R5 = Rotary Potentiometer (Small) [maximum_resistance=100kΩ package=THT]
  J1 = female pin header, 6 pins [form="♀ (female)"]

nets (from the schematic view):
  N1: Part1.A0, R5.wiper
  N2: Part1.D8, U2.DB4
  N3: Part1.D9_PWM, U2.DB7
  N4: Part1.D12/MISO, U2.RS
  N5: Part1.D13/SCK, U2.E
  GND: Part1.GND, U2.VSS, U2.R_W, U2.K, R4.CW, R5.leg1, J1.pin2, J1.pin4, J1.pin6
  N6: Part1.D2, J1.pin1
  N7: Part1.D3_PWM, J1.pin3
  N8: Part1.D4, J1.pin5
  N9: Part1.D6_PWM, U2.DB6
  N10: Part1.D7, U2.DB5
  5V: Part1.5V, U2.VDD, R1.Pin_0, R4.CCW, R5.leg2
  N11: U2.VO, R4.WIPER
  N12: U2.A, R1.Pin_1
