# Fritzing sketch arduinoBluefruitL298 (saved by Fritzing 0.9.3b)
breadboards: 1

parts:
  U3 = L298 [package=multiwatt15]
  J1 = female pin header, 5 pins [form="♀ (female)"]
  J2 = female pin header, 14 pins [form="♀ (female)"]
  Part1 = Arduino Uno (Rev3)
  IC2 = DIP - 8 pins [chip_label=IC package="DIP (Dual Inline) [THT]"]

nets:
  N1: U3.CSA, IC2.pin7
  N2: U3.OUT4, IC2.pin5
  N3: J1.pin1, Part1.D7
  N4: J1.pin2, Part1.D8
  N5: J1.pin3, Part1.D11_PWM/MOSI
  N6: J1.pin4, Part1.D12/MISO
  N7: J1.pin5, Part1.D13/SCK
  N8: J2.pin4, IC2.pin1
  N9: J2.pin7, IC2.pin3
  N10: Part1.D0/RX, IC2.pin4
  N11: Part1.D6_PWM, IC2.pin6

notes:
  Adafruit Bluefruit SPI module
  Generic L298 H-Bridge module

custom parts:
  DIP - 8 pins: A DIP stand-in part for whatever IC you want. With 8 pins on a 300mil dual inline package (DIP) footprint.
