# Fritzing sketch arduino5VDipRelay9VBatteryMotor (saved by Fritzing 0.9.2b)
breadboards: 1

parts:
  Relay = DS2 DIP Relay, DPDT 8 pins in a 16 pin size DIP [package="DIP (Dual Inline) [THT]"]
  Part1 = Arduino Uno (Rev3)
  D2 = Rectifier Diode [part_number=1N4148 package="300 mil [THT]"]
  VCC1 = Battery block 9V
  M1 = DC Motor

nets:
  N1: Relay.Coil_+, Part1.D6_PWM, D2.cathode
  N2: Relay.A_Switch_Common, M1.pin_1
  N3: Relay.A_Switch_NO, VCC1.+
  N4: Relay.Coil_-, Part1.GND, D2.anode
  N5: VCC1.-, M1.pin_2

custom parts:
  DS2 DIP Relay, DPDT 8 pins in a 16 pin size DIP: Relay, DPDT 8 pins in a 16 pin size DIP, 300mil pitch, DS2 family
