# Fritzing sketch arduino5VRelay (saved by Fritzing 0.9.0b)
breadboards: 1

parts:
  Arduino1 = Arduino Uno (Rev3)
  VCC1 = Battery block 9V
  Electronic_Toy = mystery part, 2 pins [chip_label=?]
  U1 = RELAY [package=relay-t9a]

nets:
  N1: Arduino1.D11_PWM/MOSI, U1.COIL1
  N2: Arduino1.GND, VCC1.-, U1.COIL2, U1.NO
  N3: VCC1.+, Electronic_Toy.pin1
  N4: Electronic_Toy.pin2, U1.MAIN
