# Fritzing sketch arduinoAnalogInput (saved by Fritzing 0.8.7b)
breadboards: 1

parts:
  LED1 = LED - 5mm [color="Red (633nm)" package="5 mm [THT]"]
  R3 = Resistor [tolerance=±5% resistance=470 package=THT]
  Arduino1 = Arduino Uno (Rev3)
  R2 = Resistor [tolerance=±5% resistance=10k package=THT]
  R1 = Photocell (LDR) [package=THT]

nets:
  N1: LED1.cathode, R3.Pin_0
  N2: LED1.anode, Arduino1.D10_PWM/SS
  N3: R3.Pin_1, Arduino1.GND, R2.Pin_1
  N4: Arduino1.A0, R2.Pin_0, R1.pin_0

notes:
  Arduino->File->Examples->Analog->AnalogInput
