# Fritzing sketch arduinoAnalogInputPiezo (saved by Fritzing 0.8.7b)
breadboards: 1

parts:
  Arduino1 = Arduino Uno (Rev3)
  R2 = Resistor [tolerance=±5% resistance=10k package=THT]
  R1 = Photocell (LDR) [package=THT]
  J1 = Piezo Speaker

nets:
  N1: Arduino1.A0, R2.Pin_0, R1.pin_0
  N2: Arduino1.D10_PWM/SS, J1.pin2
  N3: Arduino1.5V, R1.pin_1
  N4: Arduino1.GND, R2.Pin_1, J1.pin1

notes:
  Arduino->File->Examples->Analog->AnalogInput
