# Fritzing sketch arduinoMotor5V (saved by Fritzing 0.9.3b)
breadboards: 1

parts:
  M1 = DC Motor
  Arduino1 = Arduino Uno (Rev3)
  S1 = Pushbutton [package="[THT]"]
  R2 = Resistor [tolerance=±5% resistance=10k package=THT]
  R3 = Resistor [tolerance=±5% resistance=10k package=THT]
  Q1 = Basic FET N-Channel [package="TO220 [THT]"]
  R4 = Photocell (LDR) [package=THT]

nets:
  N1: M1.pin_1, Arduino1.D2, Arduino1.5V, S1.Pin_1, S1.Pin_2, S1.Pin_3, S1.Pin_4, R2.Pin_0, R4.pin_0
  N2: M1.pin_2, Q1.drain
  N3: Arduino1.A0, R3.Pin_0, R4.pin_1
  N4: Arduino1.GND, R2.Pin_1, R3.Pin_1, Q1.source
  N5: Arduino1.D3_PWM, Q1.gate

notes:
  N channel MOSFET e.g. RFP 12N10L or IRLB 8721
