# Fritzing sketch arduinoMotorVin (saved by Fritzing 0.9.0b)
breadboards: 1

parts:
  M1 = DC Motor
  Arduino1 = Arduino Uno (Rev3)
  Q1 = Basic FET N-Channel [package="TO220 [THT]"]

nets:
  N1: M1.pin_1, Arduino1.VIN
  N2: M1.pin_2, Q1.drain
  N3: Arduino1.D11_PWM/MOSI, Q1.gate
  N4: Arduino1.GND, Q1.source

notes:
  N channel MOSFET e.g. RFP 12N10L or IRLB 8721
