# Fritzing sketch arduinoToyBattery (saved by Fritzing 0.9.0b)
breadboards: 1

parts:
  Arduino1 = Arduino Uno (Rev3)
  Q1 = Basic FET N-Channel [package="TO220 [THT]"]
  VCC1 = Battery block 9V
  Electronic_Toy = mystery part, 2 pins [chip_label=?]
  R1 = Resistor [tolerance=±5% resistance=10k package=THT]

nets:
  N1: Arduino1.D11_PWM/MOSI, Q1.gate, R1.Pin_0
  N2: Arduino1.GND, Q1.source, VCC1.-, R1.Pin_1
  N3: Q1.drain, Electronic_Toy.pin2
  N4: VCC1.+, Electronic_Toy.pin1

notes:
  N channel MOSFET e.g. 2N7000
