# Fritzing sketch digitalPot555Theremin (saved by Fritzing 0.8.7b)
breadboards: 1

parts:
  U2 = 555 Timer [package="DIP8 [THT]"]
  R2 = Resistor [tolerance=±5% resistance=100k package=THT]
  C5 = Ceramic Capacitor [capacitance=0.1mF package="100 mil [THT, multilayer]"]
  SPKR1 = Loudspeaker
  Part1 = Arduino Uno (Rev3)
  U3 = MCP41xxx [package=so08]
  R3 = Resistor [tolerance=±5% resistance=10k package=THT]

nets:
  GND: U2.Ground, C5.0, SPKR1.pin2, Part1.GND, U3.GND
  N1: U2.Trigger, U2.Threshold, C5.1, U3.A
  N2: U2.Output, SPKR1.pin1
  5V: U2.Reset, U2.Vcc_Supply_Voltage, Part1.5V, U3.VCC
  N3: U2.Discharge, R2.Pin_0
  N4: Part1.D10_PWM/SS, U3.CS
  N5: Part1.D11_PWM/MOSI, U3.DI
  N6: Part1.D13/SCK, U3.SCK
  N7: U3.B, R3.Pin_0
