# Fritzing sketch classSample (saved by Fritzing 0.9.3b)
circuit board: 8.46667cm x 5.64444cm
breadboards: 1

parts:
  R1 = Resistor [tolerance=±5% resistance=1k package=THT]
  LED1 = LED - 5mm [color="Red (633nm)" package="5 mm [THT]"]
  Part1 = Arduino Uno (Rev3)
  R2 = Resistor [tolerance=±5% resistance=1k package=THT]
  LED2 = LED - 5mm [color="Red (633nm)" package="5 mm [THT]"]

nets:
  N1: R1.Pin_0, LED1.anode
  N2: R1.Pin_1, Part1.D11_PWM/MOSI
  N3: LED1.cathode, Part1.GND, LED2.cathode
  N4: Part1.D12/MISO, R2.Pin_1
  N5: R2.Pin_0, LED2.anode
