# Fritzing sketch combinedResistance (saved by Fritzing 0.9.0b)
breadboards: 1

parts:
  Part1 = Arduino Uno (Rev3)
  R5 = Resistor [tolerance=±5% resistance=680 package=THT]
  R3 = Resistor [tolerance=±5% resistance=220 package=THT]  # not connected
  LED6 = LED - 5mm [color="Red (633nm)" package="5 mm [THT]"]
  R4 = Resistor [tolerance=±5% resistance=1.2k package=THT]
  R6 = Resistor [tolerance=±5% resistance=560 package=THT]
  LED7 = LED - 5mm [color="Red (633nm)" package="5 mm [THT]"]
  R1 = Resistor [tolerance=±5% resistance=10 package=THT]
  R2 = Resistor [tolerance=±5% resistance=10 package=THT]  # not connected
  LED8 = LED - 5mm [color="Red (633nm)" package="5 mm [THT]"]
  LED9 = LED - 5mm [color="Red (633nm)" package="5 mm [THT]"]  # not connected

nets:
  N1: Part1.D12/MISO, LED7.anode
  N2: Part1.GND, R4.Pin_1, R6.Pin_1, R1.Pin_1, LED8.cathode
  N3: Part1.D0/RX, LED6.anode
  N4: R5.Pin_0, R4.Pin_0
