# Fritzing sketch dualMosfetMotors (saved by Fritzing 0.8.7b)

parts:
  Arduino_or_any_other_controller = Arduino Uno (Rev3)
  Q1 = Basic FET P-Channel [package="TO220 [THT]"]
  Q2 = Basic FET P-Channel [package="TO220 [THT]"]
  Motor_or_other_load = DC Motor
  Motor_or_other_load1 = DC Motor
  VCC1 = Battery  # not connected
  Part1 = Arduino ProtoShield
  JP1 = Header 2 [package=screwterminal-3.5mm-2_lock]  # not connected
  J2 = Screw terminal - 2 pins [package=THT]
  J3 = Screw terminal - 2 pins [package=THT]  # not connected

nets:
  N1: Arduino_or_any_other_controller.D9_PWM, Q2.gate, Part1.N$139
  GND: Arduino_or_any_other_controller.GND, Q1.source, Q2.source, Part1.GND, Part1.N$117
  N2: Arduino_or_any_other_controller.D5_PWM, Q1.gate
  N3: Arduino_or_any_other_controller.VIN, Motor_or_other_load.pin_1, Motor_or_other_load1.pin_1, Part1.N$19, J2.pin1
  N4: Q1.drain, Motor_or_other_load.pin_2
  N5: Q2.drain, Motor_or_other_load1.pin_2, Part1.N$4, Part1.N$128, J2.pin2

notes:
  Using a power transistor with an Arduino will allow you to control outputs that need more current or higher voltages than the Arduino can provide. Related example: http://itp.nyu.edu/physcomp/
  Tutorials/HighCurrentLoads

// code stored in the sketch: npnPowerTransistor.ino
const int transistorPin = 9;    // connected to the base of the transistor

 void setup() {
   // set  the transistor pin as output:
   pinMode(transistorPin, OUTPUT);
 }

 void loop() {
   digitalWrite(transistorPin, HIGH);
   delay(1000);
   digitalWrite(transistorPin, LOW);
   delay(1000);
 }
