# Fritzing sketch ATmega328_L293_recovered (saved by Fritzing 0.9.0b)
circuit board: 7.68668cm x 7.12387cm

parts:
  R1 = Resistor [tolerance=±5% resistance=1k package=THT]
  R3 = Resistor [tolerance=±5% resistance=10k package=THT]
  Vmotor = Screw terminal - 2 pins [package=THT]
  7-12V_input = Screw terminal - 2 pins [package=THT]
  5V_input = Screw terminal - 2 pins [package=THT]
  R2 = Resistor [tolerance=±5% resistance=1k package=THT]
  xtal = female pin header, 2 pins [form="♀ (female)"]
  1_uF = female pin header, 2 pins [form="♀ (female)"]
  Motor2 = Screw terminal - 2 pins [package=THT]
  Motor1 = Screw terminal - 2 pins [package=THT]
  0_1_uF = female pin header, 2 pins [form="♀ (female)"]
  7805 = female pin header, 3 pins [form="♀ (female)"]
  0_1_uF_2 = female pin header, 2 pins [form="♀ (female)"]
  Power_LED = female pin header, 2 pins [form="♀ (female)"]
  Programming_Header = female pin header, 6 pins [form="♀ (female)"]
  22_pF = female pin header, 2 pins [form="♀ (female)"]
  22_pF_2 = female pin header, 2 pins [form="♀ (female)"]
  C1 = female pin header, 2 pins [form="♀ (female)"]
  pin_13_LED = female pin header, 2 pins [form="♀ (female)"]
  0_1_uF1 = female pin header, 2 pins [form="♀ (female)"]
  L293 = IC, DIP package, 16 pins [chip_label=IC]
  IC1 = IC, DIP package, 28 pins [chip_label=IC]
  100_uF = female pin header, 2 pins [form="♀ (female)"]

nets:
  5V: R1.Pin_0, R3.Pin_0, 5V_input.pin1, 7805.pin3, 0_1_uF_2.pin2, C1.pin1, L293.pin16, IC1.pin7, IC1.pin20, 100_uF.pin2
  N1: R1.Pin_1, Power_LED.pin1
  N2: R3.Pin_1, 1_uF.pin2, IC1.pin1
  Vmotor: Vmotor.pin1, 0_1_uF1.pin2, L293.pin8
  GND: Vmotor.pin2, 7-12V_input.pin2, 5V_input.pin2, 0_1_uF.pin1, 7805.pin2, 0_1_uF_2.pin1, Power_LED.pin2, Programming_Header.pin5, Programming_Header.pin6, 22_pF.pin2, 22_pF_2.pin2, C1.pin2, pin_13_LED.pin2, 0_1_uF1.pin1, L293.pin4, L293.pin5, L293.pin12, L293.pin13, IC1.pin8, IC1.pin22, 100_uF.pin1
  N3: 7-12V_input.pin1, 0_1_uF.pin2, 7805.pin1
  N4: R2.Pin_0, IC1.pin19
  N5: R2.Pin_1, pin_13_LED.pin1
  N6: xtal.pin1, 22_pF.pin1, IC1.pin10
  N7: xtal.pin2, 22_pF_2.pin1, IC1.pin9
  N8: 1_uF.pin1, Programming_Header.pin1
  N9: Motor2.pin1, L293.pin14
  N10: Motor2.pin2, L293.pin11
  N11: Motor1.pin1, L293.pin3
  N12: Motor1.pin2, L293.pin6
  N13: Programming_Header.pin2, IC1.pin3
  N14: Programming_Header.pin3, IC1.pin2
  D3: L293.pin1, IC1.pin5
  D8: L293.pin2, IC1.pin14
  D9: L293.pin7, IC1.pin15
  D5: L293.pin9, IC1.pin11
  D10: L293.pin10, IC1.pin16
  D11: L293.pin15, IC1.pin17
  D2: IC1.pin4
  D4: IC1.pin6
  D6: IC1.pin12
  D7: IC1.pin13
  D12: IC1.pin18
  A0: IC1.pin23
  A1: IC1.pin24
  A2: IC1.pin25
  A3: IC1.pin26
  A4: IC1.pin27
  A5: IC1.pin28

notes:
  Power Section
  Motor Controller
  Arduino core
