# Fritzing sketch l293d_5V_twoMotors (saved by Fritzing 0.9.3b)
breadboards: 1

parts:
  M1 = DC Motor
  Part1 = Arduino Uno (Rev3)
  IC2 = H-Bridge [package=THT]
  M2 = DC Motor

nets:
  N1: M1.pin_1, IC2.1Y
  N2: M1.pin_2, IC2.2Y
  N3: Part1.D12/MISO, IC2.2A
  GND: Part1.GND, IC2.GND1, IC2.GND2, IC2.GND3, IC2.GND4
  N4: Part1.D6_PWM, IC2.1_2EN
  N5: Part1.D7, IC2.1A
  N6: Part1.5V, IC2.VCC2, IC2.VCC1
  N7: IC2.3Y, M2.pin_2
  N8: IC2.4Y, M2.pin_1

notes:
  Arduino pin 2
  Arduino pin 3
  Arduino pin 4
