# Fritzing sketch l293d_novin_second_motor (saved by Fritzing 0.9.2b)
breadboards: 1

parts:
  IC1 = L293D [package=THT]
  Part1 = Arduino Uno (Rev3)
  M2 = DC Motor
  VCC1 = Battery block 9V

nets:
  N1: IC1.0V, Part1.GND, VCC1.-
  N2: IC1.+Vmotor, VCC1.+
  N3: IC1.Enable_2, Part1.D9_PWM
  N4: IC1.In_3, Part1.D8
  N5: IC1.Out_3_(_Controlled_by_Enable_2_), M2.pin_2
  N6: IC1.Out_4_(_Controlled_by_Enable_2_), M2.pin_1
  N7: IC1.In_4, Part1.D7
  N8: IC1.+V, Part1.5V
