# Fritzing sketch l293d_vin (saved by Fritzing 0.9.2b)
breadboards: 1

parts:
  IC1 = L293D [package=THT]
  M1 = DC Motor
  Part1 = Arduino Uno (Rev3)

nets:
  N1: IC1.Enable_1, Part1.D6_PWM
  N2: IC1.In_1, Part1.D7
  N3: IC1.Out_1_(_Controlled_by_Enable_1_), M1.pin_1
  N4: IC1.0V, Part1.GND
  N5: IC1.Out_2_(_Controlled_by_Enable_1_), M1.pin_2
  N6: IC1.In_2, Part1.D12/MISO
  N7: IC1.+Vmotor, Part1.VIN
  N8: IC1.+V, Part1.5V
