# Fritzing sketch l293d_vin_two_motors (saved by Fritzing 0.9.2b)
breadboards: 1

parts:
  IC1 = L293D [package=THT]
  M1 = DC Motor
  Part1 = Arduino Uno (Rev3)
  M2 = DC Motor

nets:
  N1: IC1.Enable_1, Part1.D6_PWM
  N2: IC1.In_1, Part1.D7
  N3: IC1.Out_1_(_Controlled_by_Enable_1_), M1.pin_1
  N4: IC1.0V, Part1.GND
  N5: IC1.Out_2_(_Controlled_by_Enable_1_), M1.pin_2
  N6: IC1.In_2, Part1.D12/MISO
  N7: IC1.+Vmotor, Part1.VIN
  N8: IC1.Enable_2, Part1.D3_PWM
  N9: IC1.In_3, Part1.D4
  N10: IC1.Out_3_(_Controlled_by_Enable_2_), M2.pin_2
  N11: IC1.Out_4_(_Controlled_by_Enable_2_), M2.pin_1
  N12: IC1.In_4, Part1.D2
  N13: IC1.+V, Part1.5V
