# Fritzing sketch potAndTwoLedsSchematic (saved by Fritzing 0.9.3b)
breadboards: 1

parts:
  R5 = TRIMPOT [package=3362u-2]
  LED2 = LED - 5mm [color="Red (633nm)" package="5 mm [THT]"]
  R6 = Resistor [tolerance=±5% resistance=10k package=THT]
  LED3 = LED - 5mm [color="Red (633nm)" package="5 mm [THT]"]
  R7 = Resistor [tolerance=±5% resistance=10k package=THT]

nets:
  5V: R5.CCW
  GND: R5.CW, LED2.cathode, LED3.cathode
  N1: LED2.anode, R6.Pin_0
  Arduino digital pin 3: R6.Pin_1
  N2: LED3.anode, R7.Pin_0
  Arduino digital pin 5: R7.Pin_1
