# Fritzing sketch ATmega328_L293 (saved by Fritzing 0.9.2b)
circuit board: 7.68668cm x 7.12387cm

parts:
  R1 = Resistor [tolerance=±5% resistance=1k package=THT]
  R3 = Resistor [tolerance=±5% resistance=10k package=THT]
  Vmotor = Screw terminal - 2 pins [package=THT]
  7-12V_input = Screw terminal - 2 pins [package=THT]
  5V_input = Screw terminal - 2 pins [package=THT]
  R2 = Resistor [tolerance=±5% resistance=1k package=THT]
  xtal = female pin header, 2 pins [form="♀ (female)"]
  1_uF = female pin header, 2 pins [form="♀ (female)"]
  Motor2 = Screw terminal - 2 pins [package=THT]
  Motor1 = Screw terminal - 2 pins [package=THT]
  0_1_uF = female pin header, 2 pins [form="♀ (female)"]
  7805 = female pin header, 3 pins [form="♀ (female)"]
  0_1_uF_2 = female pin header, 2 pins [form="♀ (female)"]
  Power_LED = female pin header, 2 pins [form="♀ (female)"]
  Programming_Header = female pin header, 6 pins [form="♀ (female)"]
  22_pF = female pin header, 2 pins [form="♀ (female)"]
  22_pF_2 = female pin header, 2 pins [form="♀ (female)"]
  C1 = female pin header, 2 pins [form="♀ (female)"]
  pin_13_LED = female pin header, 2 pins [form="♀ (female)"]
  0_1_uF1 = female pin header, 2 pins [form="♀ (female)"]
  L293 = IC, DIP package, 16 pins [chip_label=IC]
  100_uF = female pin header, 2 pins [form="♀ (female)"]
  U1 = atmega328 [package=dip]

nets:
  5V: R1.Pin_0, R3.Pin_0, 5V_input.pin1, 7805.pin3, 0_1_uF_2.pin2, C1.pin1, L293.pin16, 100_uF.pin2, U1.AVCC
  N1: R1.Pin_1, Power_LED.pin1
  N2: R3.Pin_1, U1.RESET
  Vmotor: Vmotor.pin1, 0_1_uF1.pin2, L293.pin8
  GND: Vmotor.pin2, 7-12V_input.pin2, 5V_input.pin2, 0_1_uF.pin1, 7805.pin2, 0_1_uF_2.pin1, Power_LED.pin2, Programming_Header.pin5, Programming_Header.pin6, 22_pF.pin2, 22_pF_2.pin2, C1.pin2, pin_13_LED.pin2, 0_1_uF1.pin1, L293.pin4, L293.pin5, L293.pin12, L293.pin13, 100_uF.pin1, U1.GND
  N3: 7-12V_input.pin1, 0_1_uF.pin2, 7805.pin1
  N4: R2.Pin_0, U1.D13
  N5: R2.Pin_1, pin_13_LED.pin1
  N6: xtal.pin1, 22_pF.pin1, U1.XLAT2
  N7: xtal.pin2, 22_pF_2.pin1, U1.XLAT1
  N8: 1_uF.pin1, Programming_Header.pin1
  N9: Motor2.pin1, L293.pin14
  N10: Motor2.pin2, L293.pin11
  N11: Motor1.pin1, L293.pin3
  N12: Motor1.pin2, L293.pin6
  D3: L293.pin1, U1.D3_(PWM)
  D8: L293.pin2, U1.D8
  D9: L293.pin7, U1.D9_(PWM)
  D5: L293.pin9, U1.D5_(PWM)
  D10: L293.pin10, U1.D10_(PWM)
  D11: L293.pin15, U1.D11_(PWM)
  D2: U1.D2
  D4: U1.D4
  D6: U1.D6_(PWM)
  D7: U1.D7
  D12: U1.D12
  A0: U1.A0
  A1: U1.A1
  A2: U1.A2
  A3: U1.A3
  A4: U1.A4
  A5: U1.A5

notes:
  Power Section
  Motor Controller
  Arduino core
