# Fritzing sketch thereminschematic (saved by Fritzing 0.7.11b)
breadboards: 1

parts:
  Arduino1 = Arduino
  R2 = Photocell (LDR) [package=THT]
  J1 = Piezo Speaker
  R3 = Resistor [tolerance=±5% resistance=220 package=THT]
  R1 = Resistor [tolerance=±5% resistance=10k package=THT]

nets:
  N1: Arduino1.GND, J1.pin1, R1.Pin_1
  N2: Arduino1.D8, R3.Pin_1
  N3: Arduino1.+5V, R2.pin_0
  N4: R2.pin_1, R1.Pin_0
  N5: J1.pin2, R3.Pin_0
