# Fritzing sketch tooMuchLoad (saved by Fritzing 0.9.0b)
breadboards: 1

parts:
  Part1 = Arduino Uno (Rev3)
  LED1 = LED - 5mm [color="Red (633nm)" package="5 mm [THT]"]
  R1 = Resistor [tolerance=±5% resistance=680 package=THT]
  LED2 = LED - 5mm [color="Red (633nm)" package="5 mm [THT]"]
  LED3 = LED - 5mm [color="Red (633nm)" package="5 mm [THT]"]
  R2 = Resistor [tolerance=±5% resistance=560 package=THT]
  R3 = Resistor [tolerance=±5% resistance=980 package=THT]
  LED4 = LED - 5mm [color="Red (633nm)" package="5 mm [THT]"]
  LED5 = LED - 5mm [color="Red (633nm)" package="5 mm [THT]"]
  R4 = Resistor [tolerance=±5% resistance=10 package=THT]
  M1 = DC Motor
  SPKR1 = Loudspeaker
  R5 = Resistor [tolerance=±5% resistance=105 package=THT]
  LED6 = LED - 5mm [color="Red (633nm)" package="5 mm [THT]"]
  R6 = Resistor [tolerance=±5% resistance=1.2k package=THT]
  R7 = Resistor [tolerance=±5% resistance=1.5k package=THT]
  R8 = Resistor [tolerance=±5% resistance=220 package=THT]

nets:
  N1: Part1.GND, R1.Pin_1, LED3.cathode, R2.Pin_1, R4.Pin_1, M1.pin_2, R8.Pin_1
  N2: Part1.D0/RX, M1.pin_1
  N3: Part1.D1/TX, LED6.anode
  N4: Part1.D2, LED4.anode
  N5: Part1.D3_PWM, R3.Pin_0
  N6: Part1.D4, LED1.anode
  N7: Part1.D5_PWM, R5.Pin_0
  N8: LED2.cathode, R2.Pin_0
  N9: LED3.anode, R3.Pin_1
  N10: LED5.cathode, R4.Pin_0
  N11: SPKR1.pin1, R5.Pin_1
  N12: R6.Pin_0, R7.Pin_0
  N13: R6.Pin_1, R7.Pin_1
