# Fritzing sketch lm386Amplifier (saved by Fritzing 0.9.3b)
circuit board: 8.46667cm x 5.64444cm
breadboards: 1

parts:
  U1 = LM386 [package=dip08]
  R1 = Resistor [tolerance=±5% resistance=10 package=THT]
  C1 = Ceramic Capacitor [capacitance=10nF package="100 mil [THT, multilayer]"]
  C2 = Electrolytic Capacitor [capacitance=122µF package="100 mil [THT, electrolytic]"]
  J1 = Piezo Speaker
  R2 = Rotary Potentiometer (Small) [maximum_resistance=10kΩ package=THT]
  C3 = Ceramic Capacitor [capacitance=0.47mF package="200 mil [THT, multilayer]"]
  C4 = Electrolytic Capacitor [capacitance=122µF package="100 mil [THT, electrolytic]"]

nets:
  GND: U1.-IN, U1.V-, R1.Pin_1, J1.pin2, R2.leg2, C4.-
  N1: U1.+IN, C1.1
  N2: U1.OUT, C2.+, C3.1
  5V: U1.V+, C4.+
  N3: R1.Pin_0, C3.0
  N4: C1.0, R2.wiper
  N5: C2.-, J1.pin1
  Input: R2.leg1

notes:
  0.047 uF
  220 uF
  100 uF
