# Fritzing sketch 555ThereminSingleSided (saved by Fritzing 0.9.2b)
circuit board: 3.3511cm x 1.52757cm
breadboards: 1

parts:
  J1 = Piezo Speaker
  R2 = Resistor [tolerance=±5% resistance=1k package=THT]
  C1 = Ceramic Capacitor [capacitance=100nF package="100 mil [THT, multilayer]"]
  C2 = Electrolytic Capacitor [capacitance=10µF package="100 mil [THT, electrolytic]"]
  R3 = PHOTOCELL [package=photocell-kit]
  U1 = 555 Timer [package="DIP8 [THT]"]
  VCC1 = Battery block 9V

nets:
  N1: J1.pin1, C2.-
  GND: J1.pin2, C1.0, U1.Ground, VCC1.-
  N2: R2.Pin_0, R3.P$2, U1.Discharge
  N3: R2.Pin_1, C1.1, U1.Trigger, U1.Threshold
  N4: C2.+, U1.Output
  N5: R3.P$1, U1.Reset, U1.Vcc_Supply_Voltage, VCC1.+

notes:
  Piezo Speaker
  LDR or Photoresistor
