# Fritzing sketch basic555Blinker (saved by Fritzing 0.9.2b)
breadboards: 1

parts:
  U1 = 555 Timer [package="DIP8 [THT]"]
  LED1 = LED - 5mm [color="Red (633nm)" package="5 mm [THT]"]
  R1 = Resistor [tolerance=±5% resistance=220 package=THT]
  C1 = Electrolytic Capacitor [capacitance=1µF package="100 mil [THT, electrolytic]"]
  R2 = Resistor [tolerance=±5% resistance=1k package=THT]
  R3 = Resistor [tolerance=±5% resistance=470k package=THT]

nets:
  GND: U1.Ground, R1.Pin_1, C1.-
  N1: U1.Trigger, U1.Threshold, C1.+, R3.Pin_1
  N2: U1.Output, LED1.anode
  5V: U1.Reset, U1.Vcc_Supply_Voltage, R2.Pin_0
  N3: U1.Discharge, R2.Pin_1, R3.Pin_0
  N4: LED1.cathode, R1.Pin_0
