# Fritzing sketch photoresistors (saved by Fritzing 0.9.3b)
breadboards: 1

parts:
  Q1 = LTR-301 [package=ltr-301]
  R1 = Resistor [tolerance=±5% resistance=220 package=THT]
  Q2 = LTR-301 [package=ltr-301]
  R2 = Resistor [tolerance=±5% resistance=220 package=THT]
  Q3 = LTR-301 [package=ltr-301]
  R3 = Resistor [tolerance=±5% resistance=220 package=THT]

nets:
  A2: Q1.C, R1.Pin_1
  GND: Q1.E, Q2.E, Q3.E
  5V: R1.Pin_0, R2.Pin_0, R3.Pin_0
  A1: Q2.C, R2.Pin_1
  A0: Q3.C, R3.Pin_1
