# Fritzing sketch stepperMotorAdapterMultiples (saved by Fritzing 0.9.3b)
circuit board: 11.9701cm x 9.49482cm
breadboards: 1

parts:
  J1 = female pin header, 6 pins [form="♀ (female)"]
  J3 = female pin header, 3 pins [form="♀ (female)"]
  J2 = female pin header, 3 pins [form="♀ (female)"]
  J4 = female pin header, 3 pins [form="♀ (female)"]
  J5 = female pin header, 6 pins [form="♀ (female)"]
  J6 = female pin header, 3 pins [form="♀ (female)"]
  J7 = female pin header, 6 pins [form="♀ (female)"]
  J8 = female pin header, 6 pins [form="♀ (female)"]
  J9 = female pin header, 3 pins [form="♀ (female)"]
  J10 = female pin header, 3 pins [form="♀ (female)"]
  J11 = female pin header, 3 pins [form="♀ (female)"]
  J12 = female pin header, 3 pins [form="♀ (female)"]
  J16 = female pin header, 3 pins [form="♀ (female)"]
  J17 = female pin header, 3 pins [form="♀ (female)"]
  J18 = female pin header, 6 pins [form="♀ (female)"]
  J19 = female pin header, 3 pins [form="♀ (female)"]
  J20 = female pin header, 6 pins [form="♀ (female)"]
  J21 = female pin header, 3 pins [form="♀ (female)"]
  J22 = female pin header, 3 pins [form="♀ (female)"]
  J23 = female pin header, 3 pins [form="♀ (female)"]
  J24 = female pin header, 3 pins [form="♀ (female)"]
  J25 = female pin header, 6 pins [form="♀ (female)"]
  J26 = female pin header, 6 pins [form="♀ (female)"]
  J27 = female pin header, 3 pins [form="♀ (female)"]
  J28 = female pin header, 6 pins [form="♀ (female)"]
  J29 = female pin header, 3 pins [form="♀ (female)"]
  J30 = female pin header, 3 pins [form="♀ (female)"]
  J31 = female pin header, 3 pins [form="♀ (female)"]
  J32 = female pin header, 6 pins [form="♀ (female)"]
  J33 = female pin header, 3 pins [form="♀ (female)"]
  J34 = female pin header, 3 pins [form="♀ (female)"]
  J35 = female pin header, 3 pins [form="♀ (female)"]
  J36 = female pin header, 3 pins [form="♀ (female)"]
  J37 = female pin header, 3 pins [form="♀ (female)"]
  J38 = female pin header, 3 pins [form="♀ (female)"]
  J39 = female pin header, 3 pins [form="♀ (female)"]
  J40 = female pin header, 3 pins [form="♀ (female)"]
  J41 = female pin header, 6 pins [form="♀ (female)"]
  J42 = female pin header, 6 pins [form="♀ (female)"]
  J43 = female pin header, 6 pins [form="♀ (female)"]
  J44 = female pin header, 6 pins [form="♀ (female)"]
  J45 = female pin header, 3 pins [form="♀ (female)"]

nets:
  N1: J1.pin1, J2.pin3
  N2: J1.pin2, J2.pin2
  N3: J1.pin3, J2.pin1
  N4: J1.pin4, J3.pin3
  N5: J1.pin5, J3.pin2
  N6: J1.pin6, J3.pin1
  N7: J4.pin1, J5.pin6
  N8: J4.pin2, J5.pin5
  N9: J4.pin3, J5.pin4
  N10: J5.pin1, J6.pin3
  N11: J5.pin2, J6.pin2
  N12: J5.pin3, J6.pin1
  N13: J7.pin1, J9.pin3
  N14: J7.pin2, J9.pin2
  N15: J7.pin3, J9.pin1
  N16: J7.pin4, J10.pin3
  N17: J7.pin5, J10.pin2
  N18: J7.pin6, J10.pin1
  N19: J8.pin1, J11.pin3
  N20: J8.pin2, J11.pin2
  N21: J8.pin3, J11.pin1
  N22: J8.pin4, J12.pin3
  N23: J8.pin5, J12.pin2
  N24: J8.pin6, J12.pin1
  N25: J16.pin1, J28.pin6
  N26: J16.pin2, J28.pin5
  N27: J16.pin3, J28.pin4
  N28: J17.pin1, J18.pin6
  N29: J17.pin2, J18.pin5
  N30: J17.pin3, J18.pin4
  N31: J18.pin1, J30.pin3
  N32: J18.pin2, J30.pin2
  N33: J18.pin3, J30.pin1
  N34: J19.pin1, J26.pin6
  N35: J19.pin2, J26.pin5
  N36: J19.pin3, J26.pin4
  N37: J20.pin1, J24.pin3
  N38: J20.pin2, J24.pin2
  N39: J20.pin3, J24.pin1
  N40: J20.pin4, J21.pin3
  N41: J20.pin5, J21.pin2
  N42: J20.pin6, J21.pin1
  N43: J22.pin1, J26.pin3
  N44: J22.pin2, J26.pin2
  N45: J22.pin3, J26.pin1
  N46: J23.pin1, J25.pin6
  N47: J23.pin2, J25.pin5
  N48: J23.pin3, J25.pin4
  N49: J25.pin1, J29.pin3
  N50: J25.pin2, J29.pin2
  N51: J25.pin3, J29.pin1
  N52: J27.pin1, J28.pin3
  N53: J27.pin2, J28.pin2
  N54: J27.pin3, J28.pin1
  N55: J31.pin1, J43.pin6
  N56: J31.pin2, J43.pin5
  N57: J31.pin3, J43.pin4
  N58: J32.pin1, J39.pin3
  N59: J32.pin2, J39.pin2
  N60: J32.pin3, J39.pin1
  N61: J32.pin4, J35.pin3
  N62: J32.pin5, J35.pin2
  N63: J32.pin6, J35.pin1
  N64: J33.pin1, J42.pin6
  N65: J33.pin2, J42.pin5
  N66: J33.pin3, J42.pin4
  N67: J34.pin1, J43.pin3
  N68: J34.pin2, J43.pin2
  N69: J34.pin3, J43.pin1
  N70: J36.pin1, J44.pin3
  N71: J36.pin2, J44.pin2
  N72: J36.pin3, J44.pin1
  N73: J37.pin1, J42.pin3
  N74: J37.pin2, J42.pin2
  N75: J37.pin3, J42.pin1
  N76: J38.pin1, J41.pin6
  N77: J38.pin2, J41.pin5
  N78: J38.pin3, J41.pin4
  N79: J40.pin1, J44.pin6
  N80: J40.pin2, J44.pin5
  N81: J40.pin3, J44.pin4
  N82: J41.pin1, J45.pin3
  N83: J41.pin2, J45.pin2
  N84: J41.pin3, J45.pin1
