# Fritzing sketch stepperMotorAdapters (saved by Fritzing 0.9.3b)
circuit board: 2.30421cm x 3.14525cm
breadboards: 1

parts:
  J1 = female pin header, 6 pins [form="♀ (female)"]
  J3 = female pin header, 3 pins [form="♀ (female)"]
  J2 = female pin header, 3 pins [form="♀ (female)"]

nets:
  N1: J1.pin1, J2.pin3
  N2: J1.pin2, J2.pin2
  N3: J1.pin3, J2.pin1
  N4: J1.pin4, J3.pin3
  N5: J1.pin5, J3.pin2
  N6: J1.pin6, J3.pin1
