# Fritzing sketch oneDipTopAndBottm (saved by Fritzing 0.9.3b)
circuit board: 8.46667cm x 5.64444cm
breadboards: 1

parts:
  IC1 = IC, DIP package, 8 pins [chip_label=IC]

nets:
  N1: IC1.pin1, IC1.pin3, IC1.pin4, IC1.pin5, IC1.pin6, IC1.pin8
